# Fritzing sketch MyoBionic Schematics V4 (saved by Fritzing 0.9.3b)
circuit board: 8cm x 9.4cm
breadboards: 1

parts:
  M1 = Basic Servo
  M3 = Basic Servo
  M4 = Basic Servo
  R2 = Resistor [tolerance=±5% resistance=1 package=THT]
  R3 = Resistor [tolerance=±5% resistance=1 package=THT]
  ADC1 = MCP3008 [package=dil16]
  D1 = Rectifier Diode [part_number=1N4001 package="300 mil [THT]"]
  D4 = Rectifier Diode [part_number=1N4001 package="300 mil [THT]"]
  D2 = Rectifier Diode [part_number=1N4001 package="300 mil [THT]"]
  R4 = Resistor [tolerance=±5% resistance=1 package=THT]
  M2 = Basic Servo
  R1 = Resistor [tolerance=±5% resistance=1 package=THT]
  MCU1 = Raspberry Pi Zero
  D3 = Rectifier Diode [part_number=1N4001 package="300 mil [THT]"]
  J1 = female pin header, 8 pins [form="♀ (female)"]
  R5 = Resistor [tolerance=±5% resistance=220 package=THT]
  SI = SPST Switch [package=switch-spdt_kit]

nets:
  N1: M1.gnd, ADC1.CH0, R1.Pin_0
  N2: M1.vcc, D1.cathode
  N3: M1.pulse, MCU1.pin_40
  N4: M3.gnd, R3.Pin_0, ADC1.CH2
  N5: M3.vcc, D3.cathode
  N6: M3.pulse, MCU1.pin_36
  N7: M4.gnd, ADC1.CH3, R4.Pin_0
  N8: M4.vcc, D4.cathode
  N9: M4.pulse, MCU1.pin_32
  N10: R2.Pin_0, ADC1.CH1, M2.gnd
  N11: R2.Pin_1, R3.Pin_1, ADC1.DGND, ADC1.AGND, R4.Pin_1, R1.Pin_1, J1.pin3, R5.Pin_1
  N12: ADC1.CS/SHDN, MCU1.pin_15
  N13: ADC1.Din, MCU1.pin_13
  N14: ADC1.Dout, MCU1.pin_11
  N15: ADC1.CLK, MCU1.pin_7
  N16: ADC1.VREF, ADC1.VDD, J1.pin1
  N17: D1.anode, D4.anode, D2.anode, D3.anode, J1.pin4, SI.P
  N18: D2.cathode, M2.vcc
  N19: M2.pulse, MCU1.pin_38
  N20: MCU1.pin_12, R5.Pin_0, SI.S

notes:
  MyoBionic, V4
  Wiring Key
  Blue = Servo Digital Signal
  Green/Purple = Servo Analogue Resistance
  Yellow = Servo Digital Lock
